// Logisim project cpu.circ as structural Verilog: 2 circuits, main circuit main
module main (
  input  [31:0] INSTRUCTION,
  input  CLOCK,
  output [31:0] FETCH_ADDRESS,
  output [31:0] s0_Value,
  output [31:0] s1_Value,
  output [31:0] s2_Value,
  output [31:0] ra_Value,
  output [31:0] sp_Value
);

  wire ALUSrc, and_1_out, Branch, Jump, Link, main_2_equal, MemtoReg, MemWrite, RegDst, RegWrite;
  wire [1:0] ALUop_t;
  wire [3:0] adder_1_out_2;
  wire [4:0] multiplexer_1_out, undriven;
  wire [27:0] adder_1_out, bit_extender_1_out, shifter_1_out;
  wire [31:0] adder_2_out, bit_extender_2_out, main_1_read_data_1, main_1_read_data_2, main_2_result,
       main_3_p4, multiplexer_2_out, multiplexer_3_out, multiplexer_4_out, multiplexer_5_out, shifter_2_out;

  Register #(.width(32)) PC (.D(multiplexer_4_out), .Q(FETCH_ADDRESS));  // open: en, clk, clr
  assign bit_extender_1_out = {{2{1'b0}}, INSTRUCTION[25:0]};  // Bit_Extender bit_extender_1
  Adder #(.width(32)) adder_1 (.a(32'h4), .b(FETCH_ADDRESS), .out({adder_1_out_2, adder_1_out}));  // open: cin, cout
  Shifter #(.width(28)) shifter_1 (.in(bit_extender_1_out), .\dist (5'b00010), .out(shifter_1_out));
  Multiplexer #(.width(5)) multiplexer_1 (
    .in0(undriven), .in1(INSTRUCTION[15:11]), .out(multiplexer_1_out), .sel(RegDst));  // open: en
  Cpu_Control cpu_control_1 (
    .in_1(INSTRUCTION[31:26]), .RegDst(RegDst), .Branch(Branch), .Jump(Jump), .MemtoReg(MemtoReg),
    .ALUOp(ALUop_t), .MemWrite(MemWrite), .ALUSrc(ALUSrc), .RegWrite(RegWrite), .Link(Link));  // open: MemRead
  regfile_main main_1 (
    .Read_Register_1(INSTRUCTION[25:21]), .Read_Register_2(undriven), .Write_Register(multiplexer_1_out),
    .Write_Data(multiplexer_5_out), .Write_Enable(RegWrite), .Read_Data_1(main_1_read_data_1),
    .Read_Data_2(main_1_read_data_2), .s0_Value(s0_Value), .s1_Value(s1_Value), .s2_Value(s2_Value),
    .ra_Value(ra_Value), .sp_Value(sp_Value));  // open: Clock
  assign bit_extender_2_out = {{16{INSTRUCTION[15]}}, INSTRUCTION[15:0]};  // Bit_Extender bit_extender_2
  Shifter #(.width(32)) shifter_2 (.in(bit_extender_2_out), .\dist (5'b00010), .out(shifter_2_out));
  Adder #(.width(32)) adder_2 (
    .a({adder_1_out_2, adder_1_out}), .b(shifter_2_out), .out(adder_2_out));  // open: cin, cout
  Multiplexer #(.width(32)) multiplexer_2 (
    .in0(main_1_read_data_2), .in1(bit_extender_2_out), .out(multiplexer_2_out), .sel(ALUSrc));  // open: en
  Multiplexer #(.width(32)) multiplexer_3 (
    .in0({adder_1_out_2, adder_1_out}), .in1(adder_2_out), .out(multiplexer_3_out), .sel(and_1_out));  // open: en
  and and_1 (and_1_out, Branch, main_2_equal);
  alu_main main_2 (
    .X(main_1_read_data_1), .Equal(main_2_equal), .Result(main_2_result), .Y(multiplexer_2_out));  // open: Switch, Signed_Overflow
  Multiplexer #(.width(32)) multiplexer_4 (
    .in0({adder_1_out_2, shifter_1_out}), .in1(multiplexer_3_out), .out(multiplexer_4_out), .sel(Jump));  // open: en
  // mem_main main_3: pin names not known; wires that end beside it: main_2_result, main_1_read_data_2, MemWrite, main_3_p4
  Multiplexer #(.width(32)) multiplexer_5 (
    .in0(main_3_p4), .in1(main_2_result), .out(multiplexer_5_out), .sel(MemtoReg));  // open: en

  // Other names for the same wires on the sheet: clk = CLOCK; fetch_addr[31:0] = FETCH_ADDRESS; ra[31:0] = ra_Value;
  //   s0[31:0] = s0_Value; s1[31:0] = s1_Value; s2[31:0] = s2_Value; sp[31:0] = sp_Value

  // Notes on the sheet:
  //   Output
  //   These are outputs/inputs from run.circ
  //   Inputs
  //   These are DEBUG/TEST outputs from your circuit.
endmodule

module Cpu_Control (
  input  [5:0] in_1,
  output RegDst,
  output Branch,
  output Jump,
  output MemRead,
  output MemtoReg,
  output [1:0] ALUOp,
  output MemWrite,
  output ALUSrc,
  output RegWrite,
  output Link
);

  wire comparator_1_eq, comparator_2_eq, comparator_3_eq, comparator_4_eq, comparator_5_eq, comparator_6_eq,
       comparator_7_eq, comparator_8_eq, comparator_9_eq, comparator_10_eq, comparator_11_eq,
       comparator_12_eq, comparator_13_eq, comparator_14_eq, comparator_15_eq, or_2_out, or_3_out, or_4_out,
       or_5_out, or_6_out, or_7_out, or_8_out, or_9_out, or_10_out, or_11_out, or_12_out, or_14_out,
       or_15_out, or_17_out, or_18_out, or_19_out, or_20_out, or_21_out, or_22_out, or_23_out, or_24_out,
       or_25_out, or_26_out, or_27_out, or_28_out, or_29_out, or_30_out, or_31_out, or_32_out, or_33_out,
       or_34_out, or_35_out, or_36_out;
  wire [1:0] multiplexer_1_out, multiplexer_2_out, or_1_out;

  Comparator #(.width(6), .mode("unsigned")) comparator_1 (
    .a(in_1), .b({6{1'b0}}), .eq(comparator_1_eq));  // open: gt, lt
  Comparator #(.width(6), .mode("unsigned")) comparator_2 (
    .a(in_1), .b(6'b100011), .eq(comparator_2_eq));  // open: gt, lt
  Comparator #(.width(6), .mode("unsigned")) comparator_3 (
    .a(in_1), .b(6'b101011), .eq(comparator_3_eq));  // open: gt, lt
  Comparator #(.width(6), .mode("unsigned")) comparator_4 (
    .a(in_1), .b(6'b000100), .eq(comparator_4_eq));  // open: gt, lt
  Comparator #(.width(6), .mode("unsigned")) comparator_5 (
    .a(in_1), .b(6'b000010), .eq(comparator_5_eq));  // open: gt, lt
  Comparator #(.width(6), .mode("unsigned")) comparator_6 (
    .a(in_1), .b(6'b000011), .eq(comparator_6_eq));  // open: gt, lt
  Comparator #(.width(6), .mode("unsigned")) comparator_7 (
    .a(in_1), .b(6'b000101), .eq(comparator_7_eq));  // open: gt, lt
  Comparator #(.width(6), .mode("unsigned")) comparator_8 (
    .a(in_1), .b(6'b000001), .eq(comparator_8_eq));  // open: gt, lt
  Comparator #(.width(6), .mode("unsigned")) comparator_9 (
    .a(in_1), .b(6'b001000), .eq(comparator_9_eq));  // open: gt, lt
  Comparator #(.width(6), .mode("unsigned")) comparator_10 (
    .a(in_1), .b(6'b001101), .eq(comparator_10_eq));  // open: gt, lt
  Comparator #(.width(6), .mode("unsigned")) comparator_11 (
    .a(in_1), .b(6'b001111), .eq(comparator_11_eq));  // open: gt, lt
  Comparator #(.width(6), .mode("unsigned")) comparator_12 (
    .a(in_1), .b(6'b001001), .eq(comparator_12_eq));  // open: gt, lt
  Comparator #(.width(6), .mode("unsigned")) comparator_13 (
    .a(in_1), .b(6'b001100), .eq(comparator_13_eq));  // open: gt, lt
  Comparator #(.width(6), .mode("unsigned")) comparator_14 (
    .a(in_1), .b(6'b001010), .eq(comparator_14_eq));  // open: gt, lt
  Comparator #(.width(6), .mode("unsigned")) comparator_15 (
    .a(in_1), .b(6'b001011), .eq(comparator_15_eq));  // open: gt, lt
  Multiplexer #(.width(2)) multiplexer_1 (
    .in0(2'b00), .in1(2'b01), .out(multiplexer_1_out), .sel(or_3_out));  // open: en
  Multiplexer #(.width(2)) multiplexer_2 (
    .in0(2'b00), .in1(2'b10), .out(multiplexer_2_out), .sel(comparator_1_eq));  // open: en
  assign or_1_out = multiplexer_2_out | multiplexer_1_out;  // OR_Gate or_1, 2 bits wide
  or or_2 (or_2_out, or_5_out, comparator_4_eq, comparator_2_eq, comparator_2_eq, or_9_out, comparator_1_eq);
  or or_3 (or_3_out, comparator_4_eq, or_5_out);
  Multiplexer #(.width(2)) multiplexer_3 (.in1(or_1_out), .out(ALUOp), .sel(or_2_out));  // open: in0, en
  or or_4 (or_4_out, 1'b0, comparator_2_eq, comparator_6_eq, comparator_1_eq);
  or or_5 (or_5_out, comparator_7_eq, comparator_8_eq);
  or or_6 (or_6_out, 1'b0, comparator_2_eq);
  or or_7 (or_7_out, 1'b0, comparator_2_eq, comparator_3_eq, or_8_out);
  or or_8 (or_8_out, or_10_out, comparator_10_eq, comparator_12_eq, comparator_9_eq);
  or or_9 (or_9_out, or_11_out, comparator_10_eq, comparator_12_eq, comparator_9_eq);
  or or_10 (or_10_out, comparator_15_eq, comparator_14_eq, comparator_13_eq, comparator_11_eq);
  or or_11 (or_11_out, comparator_15_eq, comparator_14_eq, comparator_13_eq, comparator_11_eq);
  buf or_12 (or_12_out, comparator_1_eq);  // OR_Gate
  Multiplexer multiplexer_4 (.in1(or_12_out), .out(RegDst), .sel(or_20_out));  // open: in0, en
  or or_13 (Jump, 1'b0, comparator_5_eq, comparator_6_eq);
  Multiplexer multiplexer_5 (.in1(or_14_out), .out(MemRead), .sel(or_21_out));  // open: in0, en
  or or_14 (or_14_out, 1'b0, comparator_2_eq);
  Multiplexer multiplexer_6 (.in1(or_6_out), .out(MemtoReg), .sel(or_22_out));  // open: in0, en
  or or_15 (or_15_out, 1'b0, comparator_3_eq);
  Multiplexer multiplexer_7 (.in1(or_15_out), .out(MemWrite), .sel(or_23_out), .en(or_23_out));  // open: in0
  Multiplexer multiplexer_8 (.in1(or_7_out), .out(ALUSrc), .sel(or_27_out));  // open: in0, en
  Multiplexer multiplexer_9 (.in1(or_4_out), .out(RegWrite), .sel(or_28_out));  // open: in0, en
  or or_16 (Link, 1'b0, comparator_6_eq);
  or or_17 (or_17_out, or_19_out, comparator_10_eq, comparator_12_eq, comparator_9_eq);
  or or_18 (or_18_out, comparator_15_eq, comparator_14_eq, comparator_13_eq, comparator_11_eq);
  or or_19 (or_19_out, comparator_15_eq, comparator_14_eq, comparator_13_eq, comparator_11_eq);
  or or_20 (or_20_out, comparator_1_eq, comparator_2_eq, comparator_6_eq, or_32_out);
  or or_21 (or_21_out, comparator_4_eq, comparator_1_eq, comparator_2_eq, comparator_3_eq, comparator_5_eq, comparator_6_eq, or_5_out, or_33_out);
  or or_22 (or_22_out, comparator_2_eq, comparator_1_eq, comparator_2_eq, or_25_out);
  or or_23 (or_23_out, comparator_3_eq, comparator_1_eq, or_5_out, comparator_2_eq, comparator_4_eq, comparator_5_eq, comparator_6_eq, or_24_out);
  or or_24 (or_24_out, or_18_out, comparator_10_eq, comparator_12_eq, comparator_9_eq);
  or or_25 (or_25_out, or_26_out, comparator_10_eq, comparator_12_eq, comparator_9_eq);
  or or_26 (or_26_out, comparator_15_eq, comparator_14_eq, comparator_13_eq, comparator_11_eq);
  or or_27 (or_27_out, comparator_1_eq, comparator_2_eq, comparator_3_eq, comparator_4_eq, or_5_out, or_17_out);
  or or_28 (or_28_out, comparator_4_eq, comparator_2_eq, comparator_1_eq, comparator_3_eq, comparator_5_eq, comparator_6_eq, or_5_out, or_8_out);
  or or_29 (or_29_out, or_31_out, comparator_10_eq, comparator_12_eq, comparator_9_eq);
  or or_30 (or_30_out, comparator_15_eq, comparator_14_eq, comparator_13_eq, comparator_11_eq);
  or or_31 (or_31_out, comparator_15_eq, comparator_14_eq, comparator_13_eq, comparator_11_eq);
  or or_32 (or_32_out, or_34_out, comparator_10_eq, comparator_12_eq, comparator_9_eq);
  or or_33 (or_33_out, or_30_out, comparator_10_eq, comparator_12_eq, comparator_9_eq);
  or or_34 (or_34_out, comparator_15_eq, comparator_14_eq, comparator_13_eq, comparator_11_eq);
  or or_35 (or_35_out, 1'b0, comparator_4_eq, or_5_out);
  Multiplexer multiplexer_10 (.in1(or_35_out), .out(Branch), .sel(or_36_out));  // open: in0, en
  or or_36 (or_36_out, comparator_1_eq, comparator_2_eq, comparator_3_eq, comparator_4_eq, comparator_5_eq, or_5_out, or_29_out);

  // Notes on the sheet:
  //   R type
  //   lw
  //   sw
  //   beq
  //   j
  //   jal
  //   bne
  //   bltzal
  //   addi
  //   ori
  //   lui
  //   addiu
  //   andi
  //   slti
  //   sltiu
endmodule
