// Logisim project regfile.circ as structural Verilog: 1 circuit, main circuit main
module main (
  input  [4:0] Read_Register_1,
  input  [4:0] Read_Register_2,
  input  [4:0] Write_Register,
  input  [31:0] Write_Data,
  input  Write_Enable,
  input  Clock,
  output [31:0] s0_Value,
  output [31:0] s1_Value,
  output [31:0] s2_Value,
  output [31:0] ra_Value,
  output [31:0] sp_Value,
  output [31:0] Read_Data_1,
  output [31:0] Read_Data_2
);

  wire registerfile_1_p1, registerfile_1_p2, registerfile_1_p4, registerfile_2_p1, registerfile_2_p4,
       registerfile_2_p8, registerfile_2_p14, registerfile_2_p16, registerfile_4_p6;

  // RegisterFile registerfile_1: pin names not known; wires that end beside it: registerfile_1_p1, registerfile_1_p2, registerfile_1_p2, registerfile_1_p4, Write_Data, Clock, Write_Enable, Write_Register, 5'b11101, {5{1'b0}}, sp_Value, ra_Value
  // RegisterFile registerfile_2: pin names not known; wires that end beside it: registerfile_2_p1, Write_Data, Clock, registerfile_2_p4, Write_Enable, registerfile_2_p4, Write_Register, registerfile_2_p8, Read_Register_1, Read_Register_2, registerfile_2_p8, Read_Data_1, Read_Data_2, registerfile_2_p14, registerfile_2_p14, registerfile_2_p16, registerfile_2_p16, registerfile_2_p1
  // RegisterFile registerfile_3: pin names not known; wires that end beside it: Write_Data, Clock, Write_Enable, Write_Register, 5'b10000, 5'b10001, s0_Value, s1_Value
  // RegisterFile registerfile_4: pin names not known; wires that end beside it: Write_Data, Clock, Write_Enable, Write_Register, 5'b10010, registerfile_4_p6, registerfile_4_p6, s2_Value

  // Other names for the same wires on the sheet: clk = Clock; ra[31:0] = ra_Value; read_data1[31:0] = Read_Data_1;
  //   read_data2[31:0] = Read_Data_2; read_reg1[4:0] = Read_Register_1; read_reg2[4:0] = Read_Register_2;
  //   s0[31:0] = s0_Value; s1[31:0] = s1_Value; s2[31:0] = s2_Value; sp[31:0] = sp_Value; write_en = Write_Enable;
  //   write_reg[4:0] = Write_Register

  // Notes on the sheet:
  //   INPUTS to your circuit
  //   DON'T CHANGE THE LOCATIONS OF THE INPUTS AND OUTPUTS!
  //   These are DEBUG/TEST outputs from your circuit.
  //   copies
  //   OUTPUTS from your circuit
endmodule
